// Logisim project instruction_memory.circ as structural Verilog: 1 circuit, main circuit instructionMemory
module instructionMemory (
  input  [11:0] PC,
  input  CLOCK,
  input  reset,
  output [7:0] Byte0,
  output [7:0] Byte1,
  output [7:0] Byte2,
  output [7:0] Byte3,
  output [7:0] Byte4,
  output [7:0] Byte5,
  output [7:0] Byte6,
  output [7:0] Byte7,
  output [7:0] Byte8,
  output [7:0] Byte9
);

  wire comparator_1_eq, demultiplexer_2_out0, demultiplexer_2_out1, demultiplexer_2_out2,
       demultiplexer_2_out3, demultiplexer_2_out4, demultiplexer_2_out5, demultiplexer_2_out6,
       demultiplexer_2_out7, demultiplexer_2_out8, demultiplexer_2_out9, or_1_out;
  wire [3:0] counter_1_q;
  wire [7:0] demultiplexer_1_out0, demultiplexer_1_out1, demultiplexer_1_out2, demultiplexer_1_out3,
       demultiplexer_1_out4, demultiplexer_1_out5, demultiplexer_1_out6, demultiplexer_1_out7,
       demultiplexer_1_out8, demultiplexer_1_out9, rom_1_data;
  wire [11:0] adder_1_out;

  Adder #(.width(12)) adder_1 (.a(PC), .b({{8{1'b0}}, counter_1_q}), .out(adder_1_out));  // open: cin, cout
  ROM #(.addrWidth(12)) rom_1 (.addr(adder_1_out), .data(rom_1_data));
  Counter #(.max('hf), .width(4)) counter_1 (
    .clr(or_1_out), .up(CLOCK), .clk(CLOCK), .Q(counter_1_q));  // open: load, count, D, carry
  Comparator #(.width(4)) comparator_1 (.a(counter_1_q), .b(4'b1010), .eq(comparator_1_eq));  // open: gt, lt
  or or_1 (or_1_out, comparator_1_eq, reset);
  Demultiplexer #(.select(4), .width(8)) demultiplexer_1 (
    .out0(demultiplexer_1_out0), .out1(demultiplexer_1_out1), .out2(demultiplexer_1_out2),
    .out3(demultiplexer_1_out3), .out4(demultiplexer_1_out4), .out5(demultiplexer_1_out5),
    .out6(demultiplexer_1_out6), .out7(demultiplexer_1_out7), .out8(demultiplexer_1_out8),
    .out9(demultiplexer_1_out9), .in(rom_1_data), .sel(counter_1_q));  // open: out10, out11, out12, out13, out14, out15
  Demultiplexer #(.select(4)) demultiplexer_2 (
    .out0(demultiplexer_2_out0), .out1(demultiplexer_2_out1), .out2(demultiplexer_2_out2),
    .out3(demultiplexer_2_out3), .out4(demultiplexer_2_out4), .out5(demultiplexer_2_out5),
    .out6(demultiplexer_2_out6), .out7(demultiplexer_2_out7), .out8(demultiplexer_2_out8),
    .out9(demultiplexer_2_out9), .in(1'b1), .sel(counter_1_q));  // open: out10, out11, out12, out13, out14, out15
  Register register_1 (.D(demultiplexer_1_out0), .en(demultiplexer_2_out0), .clk(CLOCK), .Q(Byte0));  // open: clr
  Register register_2 (.D(demultiplexer_1_out1), .en(demultiplexer_2_out1), .clk(CLOCK), .Q(Byte1));  // open: clr
  Register register_3 (.D(demultiplexer_1_out2), .en(demultiplexer_2_out2), .clk(CLOCK), .Q(Byte2));  // open: clr
  Register register_4 (.D(demultiplexer_1_out3), .en(demultiplexer_2_out3), .clk(CLOCK), .Q(Byte3));  // open: clr
  Register register_5 (.D(demultiplexer_1_out4), .en(demultiplexer_2_out4), .clk(CLOCK), .Q(Byte4));  // open: clr
  Register register_6 (.D(demultiplexer_1_out5), .en(demultiplexer_2_out5), .clk(CLOCK), .Q(Byte5));  // open: clr
  Register register_7 (.D(demultiplexer_1_out6), .en(demultiplexer_2_out6), .clk(CLOCK), .Q(Byte6));  // open: clr
  Register register_8 (.D(demultiplexer_1_out7), .en(demultiplexer_2_out7), .clk(CLOCK), .Q(Byte7));  // open: clr
  Register register_9 (.D(demultiplexer_1_out8), .en(demultiplexer_2_out8), .clk(CLOCK), .Q(Byte8));  // open: clr
  Register register_10 (.D(demultiplexer_1_out9), .en(demultiplexer_2_out9), .clk(CLOCK), .Q(Byte9));  // open: clr

  // Notes on the sheet:
  //   PC (address)
  //   Clock
endmodule
